// Digital circuit 5bit-subtractor.dig as structural Verilog
module _5bit_subtractor (
  input  [4:0] A,
  input  [4:0] B,
  output [4:0] S
);

  wire [4:0] not_1_out;

  assign not_1_out = ~B;  // Not not_1, 5 bits wide
  _5bit_adder _5bit_adder_1 (.A(A), .B(not_1_out), .Ci(1'b1), .S(S));  // open: Co
endmodule
