// Digital circuit 8bit-adder.dig as structural Verilog
module _8bit_adder (
  input  Ci,
  input  [7:0] A,
  input  [7:0] B,
  output Ci_out,
  output [7:0] S_out
);

  wire full_adder_1_c_out, full_adder_2_c_out, full_adder_3_c_out, full_adder_4_c_out, full_adder_5_c_out,
       full_adder_6_c_out, full_adder_7_c_out;

  full_adder full_adder_1 (.A(A[0]), .B(B[0]), .Ci(Ci), .S(S_out[0]), .C_out(full_adder_1_c_out));
  full_adder full_adder_2 (.A(A[1]), .B(B[1]), .Ci(full_adder_1_c_out), .S(S_out[1]), .C_out(full_adder_2_c_out));
  full_adder full_adder_3 (.A(A[2]), .B(B[2]), .Ci(full_adder_2_c_out), .S(S_out[2]), .C_out(full_adder_3_c_out));
  full_adder full_adder_4 (.A(A[3]), .B(B[3]), .Ci(full_adder_3_c_out), .S(S_out[3]), .C_out(full_adder_4_c_out));
  full_adder full_adder_5 (.A(A[4]), .B(B[4]), .Ci(full_adder_4_c_out), .S(S_out[4]), .C_out(full_adder_5_c_out));
  full_adder full_adder_6 (.A(A[5]), .B(B[5]), .Ci(full_adder_5_c_out), .S(S_out[5]), .C_out(full_adder_6_c_out));
  full_adder full_adder_7 (.A(A[6]), .B(B[6]), .Ci(full_adder_6_c_out), .S(S_out[6]), .C_out(full_adder_7_c_out));
  full_adder full_adder_8 (.A(A[7]), .B(B[7]), .Ci(full_adder_7_c_out), .S(S_out[7]), .C_out(Ci_out));

  // Other names for the same wires on the sheet: Ci_out_t = Ci; S0 = S_out[0]; S1 = S_out[1]; S2 = S_out[2];
  //   S3 = S_out[3]; S4 = S_out[4]; S5 = S_out[5]; S6 = S_out[6]; S7 = S_out[7]
endmodule
