// Digital circuit 8bit-decrementor.dig as structural Verilog
module _8bit_decrementor (
  input  [7:0] A_in,
  output [7:0] S_out
);

  _8bit_adder _8bit_adder_1 (.Ci(1'b0), .A(A_in), .B({8{1'b1}}), .S_out(S_out));  // open: Ci_out
endmodule
