// Digital circuit 8bit-incrementor.dig as structural Verilog
module _8bit_incrementor (
  input  [7:0] A_in,
  output [7:0] S_out
);

  _8bit_adder _8bit_adder_1 (.Ci(1'b0), .A(A_in), .B(8'h1), .S_out(S_out));  // open: Ci_out
endmodule
