// Digital circuit 8bit-multiplicator.dig as structural Verilog
module _8bit_multiplicator (
  input  [3:0] A,
  input  [3:0] B,
  output [7:0] P
);

  wire C_out2, C_out3, C_out4, full_adder_1_c_out, full_adder_1_s, full_adder_2_c_out, full_adder_2_s,
       full_adder_3_c_out, full_adder_4_c_out, full_adder_4_s, full_adder_5_c_out, half_adder_1_c_out,
       half_adder_2_c_out, half_adder_3_c_out, P01, P02, P03, P10, P11, P12, P13, P20, P21, P22, P23, P30,
       P31, P32, P33;

  and and_1 (P[0], A[0], B[0]);
  and and_2 (P01, A[0], B[1]);
  and and_3 (P02, A[0], B[2]);
  and and_4 (P02, A[0], B[2]);
  and and_5 (P03, A[0], B[3]);
  and and_6 (P10, A[1], B[0]);
  and and_7 (P11, A[1], B[1]);
  and and_8 (P12, A[1], B[2]);
  and and_9 (P13, A[1], B[3]);
  and and_10 (P20, A[2], B[0]);
  and and_11 (P21, A[2], B[1]);
  and and_12 (P22, A[2], B[2]);
  and and_13 (P22, A[2], B[2]);
  and and_14 (P23, A[2], B[3]);
  and and_15 (P30, A[3], B[0]);
  and and_16 (P31, A[3], B[1]);
  and and_17 (P32, A[3], B[2]);
  and and_18 (P33, A[3], B[3]);
  half_adder half_adder_1 (.A(P10), .B(P01), .S(P[1]), .C_out(half_adder_1_c_out));
  full_adder full_adder_1 (.A(P30), .B(P21), .Ci(P12), .S(full_adder_1_s), .C_out(full_adder_1_c_out));
  full_adder full_adder_2 (.A(P31), .B(P22), .Ci(P13), .S(full_adder_2_s), .C_out(full_adder_2_c_out));
  full_adder full_adder_3 (.A(P32), .B(P23), .Ci(C_out4), .S(P[5]), .C_out(full_adder_3_c_out));
  full_adder full_adder_4 (.A(P20), .B(P11), .Ci(half_adder_1_c_out), .S(full_adder_4_s), .C_out(full_adder_4_c_out));
  full_adder full_adder_5 (.A(full_adder_1_s), .B(P03), .Ci(C_out2), .S(P[3]), .C_out(full_adder_5_c_out));
  half_adder half_adder_2 (.A(full_adder_2_s), .B(C_out3), .S(P[4]), .C_out(half_adder_2_c_out));
  half_adder half_adder_3 (.A(full_adder_4_s), .B(P02), .S(P[2]), .C_out(half_adder_3_c_out));
  or or_1 (C_out2, full_adder_4_c_out, half_adder_3_c_out);
  or or_2 (C_out3, full_adder_1_c_out, full_adder_5_c_out);
  or or_3 (C_out4, full_adder_2_c_out, half_adder_2_c_out);
  half_adder half_adder_4 (.A(full_adder_3_c_out), .B(P33), .S(P[6]), .C_out(P[7]));

  // Other names for the same wires on the sheet: C_out = P[7]
endmodule
