// Digital circuit 8bit-subtractor.dig as structural Verilog
module _8bit_subtractor (
  input  [7:0] A,
  input  [7:0] B,
  output [7:0] S
);

  wire [7:0] B_inv;

  _8bit_adder _8bit_adder_1 (.Ci(1'b1), .A(A), .B(B_inv), .S_out(S));  // open: Ci_out
  assign B_inv = ~B;  // Not not_1, 8 bits wide
endmodule
