// Digital circuit CPU.dig as structural Verilog
module CPU (
  input  CLK,
  input  RST,
  output [7:0] PC_OUT,
  output [7:0] BUS_SNIFFER
);

  wire CPU_CLK, HLT, IR_Ld, is_NEG, Mar_Ld, not_1_out, Out_Ld, PC_En, PC_Ld, RegA_Ld, RegB_Ld, Z_Flag;
  wire [2:0] WBus_Sel;
  wire [3:0] OpCode, ULA_op;
  wire [6:0] OUT_reg;
  wire [7:0] ans, memory_1_data, neg_1_out;

  controller controller_1 (
    .OpCode(OpCode), .Z_Flag(Z_Flag), .RST(RST), .CLK(CPU_CLK), .Mar_Ld(Mar_Ld), .RegB_Ld(RegB_Ld),
    .RegA_Ld(RegA_Ld), .PC_Ld(PC_Ld), .HLT(HLT), .WBus_Sel(WBus_Sel), .ULA_op(ULA_op), .PC_En(PC_En),
    .IR_Ld(IR_Ld), .Out_Ld(Out_Ld));
  not not_1 (not_1_out, HLT);
  and and_1 (CPU_CLK, not_1_out, CLK);
  PC pc_1 (.PC_En(PC_En), .CLK(CPU_CLK), .WBus(BUS_SNIFFER), .PC_Ld(PC_Ld), .RST(RST), .PC_out(PC_OUT));
  memory memory_1 (.WBus(BUS_SNIFFER), .CLK(CPU_CLK), .Mar_Ld(Mar_Ld), .RST(RST), .Data(memory_1_data));
  resgistrator u_Out_Reg (.D(BUS_SNIFFER), .CLK(CPU_CLK), .Ld(Out_Ld), .RST(RST), .Q_out({is_NEG, OUT_reg}));
  data_path data_path_1 (
    .WBus(BUS_SNIFFER), .RegA_Ld(RegA_Ld), .RegB_Ld(RegB_Ld), .IR_Ld(IR_Ld), .ULA_op(ULA_op),
    .WBus_Sel(WBus_Sel), .CLK(CPU_CLK), .RST(RST), .Mem_Data(memory_1_data), .PC(PC_OUT), .OpCode(OpCode),
    .WBus_out(BUS_SNIFFER), .Z_Flag(Z_Flag));
  Neg #(.Bits(8)) neg_1 (.in({is_NEG, OUT_reg}), .out(neg_1_out));
  LED led_1 (.in(is_NEG));
  Multiplexer #(.Bits(8)) multiplexer_1 (.sel(is_NEG), .in_0({is_NEG, OUT_reg}), .in_1(neg_1_out), .out(ans));
  Seven_Seg_Hex seven_seg_hex_1 (.d(ans[7:4]), .dp(1'b0));
  Seven_Seg_Hex seven_seg_hex_2 (.d(ans[3:0]), .dp(1'b0));

  // Other names for the same wires on the sheet: OUT_reg[7] = is_NEG; WBus[7:0] = BUS_SNIFFER

  // Notes on the sheet:
  //   CLK: Hz: 3
endmodule
