// Digital circuit PC.dig as structural Verilog
module PC (
  input  PC_En,
  input  CLK,
  input  [7:0] WBus,
  input  PC_Ld,
  input  RST,
  output [7:0] PC_out
);

  CounterPreset #(.Bits(8)) counterpreset_1 (
    .en(PC_En), .C(CLK), .dir(1'b0), .in(WBus), .ld(PC_Ld), .clr(RST), .out(PC_out));  // open: ovf
endmodule
