// Digital circuit controller.dig as structural Verilog
module controller (
  input  [3:0] OpCode,
  input  Z_Flag,
  input  RST,
  input  CLK,
  output Mar_Ld,
  output RegB_Ld,
  output RegA_Ld,
  output PC_Ld,
  output HLT,
  output [2:0] WBus_Sel,
  output [3:0] ULA_op,
  output PC_En,
  output IR_Ld,
  output Out_Ld
);

  wire Add_sin, and_1_out, and_2_out, and_3_out, and_4_out, and_5_out, and_6_out, and_7_out, Dec_sin,
       Div_sin, HLT_sin, Inc_sin, Jump_sin, JumpIf_sin, LDA_sin, Mult_sin, or_1_out, or_2_out, or_3_out,
       out_1, out_2, out_3, out_4, out_5, out_sin, Sub_sin, T_1, T_4, T_5, T_6;
  wire [2:0] priorityencoder_1_num;

  Decoder #(.Selector_Bits(4)) decoder_1 (
    .sel(OpCode), .out_0(out_1), .out_1(LDA_sin), .out_2(Add_sin), .out_3(Sub_sin), .out_4(Mult_sin),
    .out_5(Div_sin), .out_6(Inc_sin), .out_7(Dec_sin), .out_8(Jump_sin), .out_9(JumpIf_sin), .out_10(out_2),
    .out_11(out_3), .out_12(out_4), .out_13(out_5), .out_14(out_sin), .out_15(HLT_sin));
  sequencer sequencer_1 (.RST(RST), .CLK(CLK), .T_1(T_1), .T_2(PC_En), .T_3(IR_Ld), .T_4(T_4), .T_5(T_5), .T_6(T_6));
  or or_1 (or_1_out, LDA_sin, Add_sin, Sub_sin, Mult_sin, Div_sin);
  and and_1 (and_1_out, LDA_sin, T_5);
  or or_2 (or_2_out, Sub_sin, Add_sin, Mult_sin, Div_sin);
  or or_3 (or_3_out, Dec_sin, Inc_sin);
  and and_2 (and_2_out, Jump_sin, T_4);
  and and_3 (and_3_out, JumpIf_sin, Z_Flag, T_4);
  and and_4 (and_4_out, or_1_out, T_4);
  and and_5 (and_5_out, or_2_out, T_6);
  and and_6 (and_6_out, T_4, or_3_out);
  or or_4 (PC_Ld, and_2_out, and_3_out);
  or or_5 (Mar_Ld, and_4_out, T_1);
  and and_7 (and_7_out, HLT_sin, T_4);
  and and_8 (RegB_Ld, T_5, or_2_out);
  or or_6 (RegA_Ld, and_1_out, and_5_out, and_6_out);
  and and_9 (Out_Ld, out_sin, T_4);
  RS_FF_AS rs_ff_as_1 (.S(and_7_out), .R(RST), .Q(HLT));  // open: nQ
  PriorityEncoder #(.Selector_Bits(3)) priorityencoder_1 (
    .in0(T_1), .in1(PC_En), .in2(IR_Ld), .in3(T_4), .in4(T_5), .in5(T_6), .in6(1'b0), .in7(1'b0),
    .num(priorityencoder_1_num));  // open: any
  ROM #(.AddrBits(7), .Bits(7)) rom_1 (.A({OpCode, priorityencoder_1_num}), .sel(1'b1), .D({ULA_op, WBus_Sel}));

  // Other names for the same wires on the sheet: T_2 = PC_En; T_3 = IR_Ld

  // Notes on the sheet:
  //   contents of rom_1 (hex, n*v repeats v):
  //   5,0,1,5*0,5,0,1,0,1,0,0,0,5,0,1,0,1,2,0,0,5,0,1,0,1,a,0,0,5,0
  //   ,1,0,1,1a,0,0,5,0,1,0,1,2a,0,0,5,0,1,32,4*0,5,0,1,3a,4*0,5,0,1
  //   ,5*0,5,0,1,37*0,5,0,1,3,4*0,5,0,1
endmodule
