// Digital circuit data-path.dig as structural Verilog
module data_path (
  input  [7:0] WBus,
  input  RegA_Ld,
  input  RegB_Ld,
  input  IR_Ld,
  input  [3:0] ULA_op,
  input  [2:0] WBus_Sel,
  input  CLK,
  input  RST,
  input  [7:0] Mem_Data,
  input  [7:0] PC,
  output [3:0] OpCode,
  output [7:0] WBus_out,
  output Z_Flag
);

  wire [3:0] IR_out;
  wire [7:0] Mem2, RegA_out, RegB_out;

  ula ula_1 (.A(RegA_out), .B(RegB_out), .OP(ULA_op), .Z(Z_Flag), .RES(Mem2));
  resgistrator resgistrator_1 (.D(WBus), .CLK(CLK), .Ld(IR_Ld), .RST(RST), .Q_out({OpCode, IR_out}));
  Register #(.Bits(8)) RegA (.D(WBus), .C(CLK), .en(RegA_Ld), .Q(RegA_out));
  Register #(.Bits(8)) RegB (.D(WBus), .C(CLK), .en(RegB_Ld), .Q(RegB_out));
  Multiplexer #(.Selector_Bits(3), .Bits(8)) multiplexer_1 (
    .sel(WBus_Sel), .in_0({4'b0000, IR_out}), .in_1(Mem_Data), .in_2(Mem2), .in_3(RegA_out), .in_4(RegB_out),
    .in_5(PC), .in_6({8{1'b0}}), .in_7({8{1'b0}}), .out(WBus_out));

  // Other names for the same wires on the sheet: Mem1[7:0] = Mem_Data; Mem5[7:0] = PC
endmodule
