// Digital circuit divisor.dig as structural Verilog
module divisor (
  input  [3:0] A,
  input  [3:0] B,
  output [3:0] R,
  output [3:0] Q
);

  wire [3:0] partial_division_1_r_out, partial_division_2_r_out, partial_division_3_r_out;

  partial_division partial_division_1 (
    .R_in(4'b0000), .A_in(A[3]), .B_in(B), .R_out(partial_division_1_r_out), .Q_out(Q[3]));
  partial_division partial_division_2 (
    .R_in(partial_division_1_r_out), .A_in(A[2]), .B_in(B), .R_out(partial_division_2_r_out), .Q_out(Q[2]));
  partial_division partial_division_3 (
    .R_in(partial_division_2_r_out), .A_in(A[1]), .B_in(B), .R_out(partial_division_3_r_out), .Q_out(Q[1]));
  partial_division partial_division_4 (.R_in(partial_division_3_r_out), .A_in(A[0]), .B_in(B), .R_out(R), .Q_out(Q[0]));

  // Other names for the same wires on the sheet: A4 = A[0]; A3 = A[1]; A1 = A[3]; B_in[3:0] = B; Q_out1 = Q[3];
  //   Q_out2 = Q[2]; Q_out3 = Q[1]; Q_out4 = Q[0]
endmodule
