// Digital circuit full-adder.dig as structural Verilog
module full_adder (
  input  A,
  input  B,
  input  Ci,
  output S,
  output C_out
);

  wire CoA_out, CoB_out, half_adder_1_s;

  half_adder half_adder_1 (.A(A), .B(B), .S(half_adder_1_s), .C_out(CoA_out));
  half_adder half_adder_2 (.A(half_adder_1_s), .B(Ci), .S(S), .C_out(CoB_out));
  or or_1 (C_out, CoA_out, CoB_out);

  // Other names for the same wires on the sheet: A_out = A; B_out = B; Ci_out = Ci; Co_out = C_out; S_out = S
endmodule
