// Digital circuit memory.dig as structural Verilog
module memory (
  input  [7:0] WBus,
  input  CLK,
  input  Mar_Ld,
  input  RST,
  output [7:0] Data
);

  wire [7:0] Mar_q;

  Register #(.Bits(8)) Mar (.D(WBus), .C(CLK), .en(Mar_Ld), .Q(Mar_q));
  ROM #(.AddrBits(8), .Bits(8)) rom_1 (.A(Mar_q), .sel(1'b1), .D(Data));

  // Notes on the sheet:
  //   contents of rom_1 (hex, n*v repeats v):
  //   1f,3e,70,e0,97,82,0,f0,6*0,5,7,224*0,3
endmodule
