// Digital circuit partial_division.dig as structural Verilog
module partial_division (
  input  [3:0] R_in,
  input  A_in,
  input  [3:0] B_in,
  output [3:0] R_out,
  output Q_out
);

  wire [3:0] M_in;
  wire [4:4] _5bit_subtractor_1_s;

  _5bit_subtractor _5bit_subtractor_1 (.A({R_in, A_in}), .B({1'b0, B_in}), .S({_5bit_subtractor_1_s[4], M_in}));
  Multiplexer #(.Bits(4)) multiplexer_1 (.sel(Q_out), .in_0({R_in[2:0], A_in}), .in_1(M_in), .out(R_out));
  not not_1 (Q_out, _5bit_subtractor_1_s[4]);

  // Other names for the same wires on the sheet: Div_partial[4:0] = {R_in, A_in}
endmodule
