// Digital circuit sequencer.dig as structural Verilog
module sequencer (
  input  RST,
  input  CLK,
  output T_1,
  output T_2,
  output T_3,
  output T_4,
  output T_5,
  output T_6
);

  wire counterpreset_1_ovf, or_1_out;
  wire [2:0] counterpreset_1_out;

  or or_1 (or_1_out, RST, counterpreset_1_ovf);
  CounterPreset #(.Bits(3), .maxValue(5)) counterpreset_1 (
    .en(1'b1), .C(CLK), .dir(1'b0), .in(3'b000), .ld(1'b0), .clr(or_1_out), .out(counterpreset_1_out),
    .ovf(counterpreset_1_ovf));
  Decoder #(.Selector_Bits(3)) decoder_1 (
    .sel(counterpreset_1_out), .out_0(T_1), .out_1(T_2), .out_2(T_3), .out_3(T_4), .out_4(T_5), .out_5(T_6));  // open: out_6, out_7
endmodule
