// Digital circuit ula.dig as structural Verilog
module ula (
  input  [7:0] A,
  input  [7:0] B,
  input  [3:0] OP,
  output Z,
  output [7:0] RES
);

  wire [7:0] Add_res, Dec_res, Div_res, Inc_res, Mult_res, Sub_res;

  nor nor_1 (Z, RES[0], RES[1], RES[2], RES[3], RES[4], RES[5], RES[6], RES[7]);
  _8bit_adder _8bit_adder_1 (.Ci(1'b0), .A(A), .B(B), .S_out(Add_res));  // open: Ci_out
  _8bit_incrementor _8bit_incrementor_1 (.A_in(A), .S_out(Inc_res));
  _8bit_multiplicator _8bit_multiplicator_1 (.A(A[3:0]), .B(B[3:0]), .P(Mult_res));
  Multiplexer #(.Bits(8), .Selector_Bits(4)) multiplexer_1 (
    .sel(OP), .in_0(Add_res), .in_1(Sub_res), .in_2(B), .in_3(Mult_res), .in_4({8{1'b0}}), .in_5(Div_res),
    .in_6(Inc_res), .in_7(Dec_res), .in_8({8{1'b0}}), .in_9({8{1'b0}}), .in_10({8{1'b0}}), .in_11({8{1'b0}}),
    .in_12({8{1'b0}}), .in_13({8{1'b0}}), .in_14({8{1'b0}}), .in_15({8{1'b0}}), .out(RES));
  _8bit_subtractor _8bit_subtractor_1 (.A(A), .B(B), .S(Sub_res));
  _8bit_decrementor _8bit_decrementor_1 (.A_in(A), .S_out(Dec_res));
  divisor divisor_1 (.A(A[3:0]), .B(B[3:0]), .R(Div_res[3:0]), .Q(Div_res[7:4]));

  // Other names for the same wires on the sheet: AL_res[7:0] = RES
endmodule
